# Fritzing sketch speedometer (saved by Fritzing 0.9.3b)

parts:
  Componente1 = Arduino Nano (Rev3.0)
  S2 = Reed switch [package=THT]
  BAT1 = 18650 battery holder [package=battery-18650-kit]
  M1 = TP4056 Module [part_number=HW-107]
  A1 = mini boost module
  U4 = SWITCH-SPST-2 [package=switch-spst-vertical]
  J1 = Basic Servo
  U5 = 7-SEGMENT-4DIGIT [package=7-segment-4digit]
  Header1 = 2 pin header [package=THT]  # not connected
  Header2 = 2 pin header [package=THT]  # not connected

nets:
  GND: Componente1.GND, A1.Pin_3, J1.gnd
  N1: Componente1.D2, S2.pin_2
  N2: Componente1.D3, J1.pulse
  N3: Componente1.D6, U5.11
  N4: Componente1.VIN, A1.Pin_4
  5V: Componente1.5V, J1.vcc
  N5: Componente1.A5, U5.14
  N6: Componente1.A4, U5.13
  N7: Componente1.3V3, S2.pin_1
  N8: BAT1.+, M1.BAT-
  N9: BAT1.-, U4.O
  N10: M1.OUT-#1, A1.Pin_1
  N11: M1.BAT+, U4.P
  N12: M1.OUT-#4, A1.Pin_2

notes:
  Bike front-wheel
  speedometer picture

custom parts:
  18650 battery holder: 18650 Battery Holder identical to the dual battery version.
  TP4056 Module: TP4056 Lithium Battery Charge Management Module Links: TP4056 website
  mini boost module: mini boost module.
  2 pin header: 2 pin male to male header
